# Fritzing sketch led_strip (saved by Fritzing 0.9.3b)
breadboards: 1

parts:
  Part1 = Arduino Nano (Rev3.0)
  Q1 = Basic FET N-Channel [package="TO220 [THT]"]

nets:
  N1: Part1.GND, Q1.source
  N2: Part1.D3, Q1.gate

notes:
  power supply
  led strip
